// Logisim project ALU.circ as structural Verilog: 1 circuit, main circuit main
module main (
  input  [3:0] A,
  input  [3:0] B,
  input  Enable,
  input  isAsr,
  input  isLsr,
  input  isLsl,
  input  isOr,
  input  isAnd,
  input  isNot,
  input  isMul,
  input  isAdd,
  input  isSub,
  input  isCmp,
  output [3:0] AluResult
);

  wire comparator_1_eq, comparator_1_gt, or_2_out;
  wire [2:0] priority_encoder_1_out;
  wire [3:0] adder_1_out, and_1_out, bit_extender_1_out, multiplier_1_out, not_1_out, or_1_out,
       shifter_1_out, shifter_2_out, shifter_3_out, xor_1_out;

  assign bit_extender_1_out = {{3{isSub}}, isSub};  // Bit_Extender bit_extender_1
  assign xor_1_out = bit_extender_1_out ^ B;  // XOR_Gate xor_1, 4 bits wide
  Adder #(.width(4)) adder_1 (.a(A), .b(xor_1_out), .out(adder_1_out), .cin(isSub));  // open: cout
  Multiplier #(.width(4)) multiplier_1 (.a(A), .b(B), .out(multiplier_1_out));  // open: cin, cout
  assign not_1_out = ~A;  // NOT_Gate not_1, 4 bits wide
  assign and_1_out = A & B;  // AND_Gate and_1, 4 bits wide
  assign or_1_out = A | B;  // OR_Gate or_1, 4 bits wide
  Shifter #(.width(4)) shifter_1 (.in(A), .\dist (B[1:0]), .out(shifter_1_out));
  Shifter #(.width(4), .shift("lr")) shifter_2 (.in(A), .\dist (B[1:0]), .out(shifter_2_out));
  Shifter #(.width(4), .shift("ar")) shifter_3 (.in(A), .\dist (B[1:0]), .out(shifter_3_out));
  Comparator #(.width(4)) comparator_1 (.a(A), .b(B), .gt(comparator_1_gt), .eq(comparator_1_eq));  // open: lt
  D_Flip_Flop Flags_E (.clk(isCmp), .D(comparator_1_eq), .en(isCmp));  // open: Q, Qn, preset, reset
  D_Flip_Flop Flags_Gt (.clk(isCmp), .D(comparator_1_gt), .en(isCmp));  // open: Q, Qn, preset, reset
  Priority_Encoder priority_encoder_1 (
    .in0(or_2_out), .in1(isMul), .in2(isNot), .in3(isAnd), .in4(isOr), .in5(isLsl), .in6(isLsr), .in7(isAsr),
    .out(priority_encoder_1_out), .en_in(Enable));
  or or_2 (or_2_out, isSub, isAdd);
  Multiplexer #(.select(3), .width(4)) multiplexer_1 (
    .in0(adder_1_out), .in1(multiplier_1_out), .in2(not_1_out), .in3(and_1_out), .in4(or_1_out),
    .in5(shifter_1_out), .in6(shifter_2_out), .in7(shifter_3_out), .out(AluResult),
    .sel(priority_encoder_1_out), .en(Enable));
endmodule
