// Logisim project FetchUnit.circ as structural Verilog: 1 circuit, main circuit main
module main (
  input  IsBranchTaken,
  input  IsRet,
  input  [3:0] BranchTarget,
  input  [1:0] Ra,
  input  [3:0] plus_1,
  input  Enable,
  input  Next_Instruction,
  input  IsStr,
  output [3:0] BranchPC,
  output [3:0] Immx,
  output [3:0] Op1,
  output [3:0] Op2
);

  wire [1:0] multiplexer_2_out, multiplexer_3_out;
  wire [3:0] adder_1_out, multiplexer_1_out, register_1_q, register_2_q, register_3_q, register_4_q,
       register_5_q;
  wire [13:4] rom_1_data;

  Register #(.width(4)) register_1 (
    .D(multiplexer_1_out), .en(Enable), .Q(register_1_q), .clk(Next_Instruction));  // open: clr
  Multiplexer #(.width(4), .enable("false")) multiplexer_1 (
    .in0(adder_1_out), .in1(BranchTarget), .out(multiplexer_1_out), .sel(IsBranchTaken));
  ROM #(.addrWidth(4), .dataWidth(14)) rom_1 (.addr(register_1_q), .data({rom_1_data, Immx}), .sel(Enable));
  Adder #(.width(4)) adder_1 (.a(plus_1), .b(register_1_q), .out(adder_1_out));  // open: cin, cout
  Register #(.width(4)) register_2 (.en(Enable), .Q(register_2_q));  // open: D, clk, clr
  Register #(.width(4)) register_3 (.en(Enable), .Q(register_3_q));  // open: D, clk, clr
  Register #(.width(4)) register_4 (.en(Enable), .Q(register_4_q));  // open: D, clk, clr
  Register #(.width(4)) register_5 (.en(Enable), .Q(register_5_q));  // open: D, clk, clr
  Adder #(.width(4)) adder_2 (.a(register_1_q), .b(Immx), .out(BranchPC));  // open: cin, cout
  Multiplexer #(.width(2)) multiplexer_2 (.in0(Immx[3:2]), .in1(Ra), .out(multiplexer_2_out), .sel(IsRet), .en(Enable));
  Multiplexer #(.width(2)) multiplexer_3 (
    .in0(rom_1_data[5:4]), .in1(rom_1_data[7:6]), .out(multiplexer_3_out), .sel(IsStr), .en(Enable));
  Multiplexer #(.select(2), .width(4)) multiplexer_4 (
    .in0(register_2_q), .in1(register_3_q), .in2(register_4_q), .in3(register_5_q), .out(Op1),
    .sel(multiplexer_2_out), .en(Enable));
  Multiplexer #(.select(2), .width(4)) multiplexer_5 (
    .in0(register_2_q), .in1(register_3_q), .in2(register_4_q), .in3(register_5_q), .out(Op2),
    .sel(multiplexer_3_out), .en(Enable));

  // Notes on the sheet:
  //   contents of rom_1 (hex, n*v repeats v):
  //   3460 372 3223 3242 44 424 324 545 346 47 2346 3467 3476 3347 747 2734
endmodule
