// Logisim project HardwiredControlUnit.circ as structural Verilog: 1 circuit, main circuit main
module main (
  input  I,
  input  op5,
  input  op4,
  input  op3,
  input  op2,
  input  op1,
  output isStr,
  output isLd,
  output isBeq,
  output isBgt,
  output isRet,
  output isImm,
  output isWb,
  output isB,
  output isCall,
  output isAdd,
  output isSub,
  output isCmp,
  output isMul,
  output isDiv,
  output isMod,
  output isLsl,
  output isLsr,
  output isAsr,
  output isOr,
  output isAnd,
  output isNot,
  output isMov
);

  wire and_1_out, and_2_out, and_3_out, and_4_out, and_5_out, and_6_out, nand_1_out, not_1_out, not_2_out,
       not_3_out, not_4_out, not_5_out, or_1_out;

  not not_1 (not_1_out, op5);
  not not_2 (not_2_out, op4);
  not not_3 (not_3_out, op3);
  not not_4 (not_4_out, op2);
  not not_5 (not_5_out, op1);
  or or_1 (or_1_out, op4, not_4_out);
  nand nand_1 (nand_1_out, op1, op3, not_1_out, or_1_out);
  and and_1 (and_1_out, op1, op2, not_3_out, not_2_out, op5);
  and and_2 (and_2_out, not_1_out, nand_1_out);
  and and_3 (and_3_out, not_5_out, not_4_out, op3, not_2_out, op5);
  and and_4 (and_4_out, op2, not_3_out, not_2_out, op5);
  and and_5 (and_5_out, not_5_out, not_4_out, not_3_out, not_2_out, not_1_out);
  and and_6 (and_6_out, op2, op3, op4, not_1_out);
  and and_7 (isStr, op1, op2, op3, op4, not_1_out);
  and and_8 (isLd, not_5_out, op2, op3, op4, not_1_out);
  and and_9 (isBeq, not_5_out, not_4_out, not_3_out, not_2_out, op5);
  and and_10 (isBgt, op1, not_4_out, not_3_out, not_2_out, op5);
  and and_11 (isRet, not_5_out, not_4_out, op3, not_2_out, op5);
  or or_2 (isWb, and_1_out, and_2_out);
  or or_3 (isB, and_3_out, and_4_out);
  and and_12 (isCall, op1, op2, not_3_out, not_2_out, op5);
  or or_4 (isAdd, and_5_out, and_6_out);
  and and_13 (isSub, op1, not_4_out, not_3_out, not_2_out, not_1_out);
  and and_14 (isCmp, op1, not_4_out, op3, not_2_out, not_1_out);
  and and_15 (isMul, not_5_out, op2, not_3_out, not_2_out, not_1_out);
  and and_16 (isDiv, op1, op2, not_3_out, not_2_out, not_1_out);
  and and_17 (isMod, not_5_out, not_4_out, op3, not_2_out, not_1_out);
  and and_18 (isLsl, not_5_out, op2, not_3_out, op4, not_1_out);
  and and_19 (isLsr, not_5_out, op2, not_3_out, op4, not_1_out);
  and and_20 (isAsr, op1, op2, not_3_out, op4, not_1_out);
  and and_21 (isOr, not_5_out, not_4_out, op3, op4, not_1_out);
  and and_22 (isAnd, op1, op2, op3, not_2_out, not_1_out);
  and and_23 (isNot, not_5_out, not_4_out, not_3_out, op4, not_1_out);
  and and_24 (isMov, op1, not_4_out, not_3_out, op4, not_1_out);

  assign isImm = I;
endmodule
